// Digital circuit 4BitAdderSubtractor.dig as structural Verilog
module _4BitAdderSubtractor (
  input  [3:0] A,
  input  [3:0] B,
  input  SUB,
  output Cout,
  output [3:0] Sum
);

  wire FA0_p5, FA1_p5, FA2_p5, xor_1_out, xor_2_out, xor_3_out, xor_4_out;

  xor xor_1 (xor_1_out, SUB, B[0]);
  // HW1_1Bit_Full_Adder FA0: pin names not known; wires that end beside it: A[0], xor_1_out, SUB, Sum[0], FA0_p5
  xor xor_2 (xor_2_out, SUB, B[1]);
  // HW1_1Bit_Full_Adder FA1: pin names not known; wires that end beside it: A[1], xor_2_out, FA0_p5, Sum[1], FA1_p5
  xor xor_3 (xor_3_out, SUB, B[2]);
  // HW1_1Bit_Full_Adder FA2: pin names not known; wires that end beside it: A[2], xor_3_out, FA1_p5, Sum[2], FA2_p5
  xor xor_4 (xor_4_out, SUB, B[3]);
  // HW1_1Bit_Full_Adder FA3: pin names not known; wires that end beside it: A[3], xor_4_out, FA2_p5, Sum[3], Cout
endmodule
