// Digital circuit 4Bit_ALU.dig as structural Verilog
module _4Bit_ALU (
  input  [3:0] A,
  input  [3:0] B,
  input  [1:0] S1S0,
  input  Cin,
  output Cout,
  output [3:0] D
);

  wire [3:0] multiplexer_1_out, not_1_out, not_2_out;

  assign not_1_out = ~B;  // Not not_1, 4 bits wide
  assign not_2_out = ~4'b0000;  // Not not_2, 4 bits wide
  Multiplexer #(.Bits(4), .Selector_Bits(2)) multiplexer_1 (
    .sel(S1S0), .in_0(B), .in_1(not_1_out), .in_2(4'b0000), .in_3(not_2_out), .out(multiplexer_1_out));
  // HW1_4Bit_RippleCarry_Adder hw1_4bit_ripplecarry_adder_1: pin names not known; wires that end beside it: A, multiplexer_1_out, Cin, D, Cout

  // Notes on the sheet:
  //   S1S0: default 1
endmodule
