// Digital circuit Register Implementation.dig as structural Verilog
module Register_Implementation (
  input  [3:0] Write_Data,
  input  [1:0] Write_Register,
  input  [1:0] Read_Register_1,
  input  [1:0] Read_Register_2,
  input  Control_Signal,
  input  CLK,
  output [3:0] Read_Data_1,
  output [3:0] Read_Data_2
);

  wire [3:0] demultiplexer_1_out_0, demultiplexer_1_out_1, demultiplexer_1_out_2, demultiplexer_1_out_3,
       R0_q, R1_q, R2_q, R3_q;

  Demultiplexer #(.Bits(4), .Selector_Bits(2)) demultiplexer_1 (
    .sel(Write_Register), .in(Write_Data), .out_0(demultiplexer_1_out_0), .out_1(demultiplexer_1_out_1),
    .out_2(demultiplexer_1_out_2), .out_3(demultiplexer_1_out_3));
  Register #(.Bits(4)) R0 (.D(demultiplexer_1_out_0), .C(CLK), .en(Control_Signal), .Q(R0_q));
  Register #(.Bits(4)) R1 (.D(demultiplexer_1_out_1), .C(CLK), .en(Control_Signal), .Q(R1_q));
  Register #(.Bits(4)) R2 (.D(demultiplexer_1_out_2), .C(CLK), .en(Control_Signal), .Q(R2_q));
  Register #(.Bits(4)) R3 (.D(demultiplexer_1_out_3), .C(CLK), .en(Control_Signal), .Q(R3_q));
  Multiplexer #(.Bits(4), .Selector_Bits(2)) multiplexer_1 (
    .sel(Read_Register_1), .in_0(R0_q), .in_1(R1_q), .in_2(R2_q), .in_3(R3_q), .out(Read_Data_1));
  Multiplexer #(.Selector_Bits(2), .Bits(4)) multiplexer_2 (
    .sel(Read_Register_2), .in_0(R0_q), .in_1(R1_q), .in_2(R2_q), .in_3(R3_q), .out(Read_Data_2));
endmodule
